# Fritzing sketch TiltingLIDARScannerPCBv1 (saved by Fritzing 0.9.2b)
circuit board: 5.72713cm x 5.11266cm
breadboards: 1

parts:
  Arduino_Micro = Arduino Nano (Rev3.0)
  Easy_Driver = EasyDriver_v44
  J1 = Power Jack [package=power_jack_smd]
  JP2 = Header 4 [package=screwterminal-3.5mm-4_lock]
  JP3 = Header 4 [package=screwterminal-3.5mm-4_lock]
  R1 = Resistor [tolerance=±5% resistance=10k package="0805 [SMD]"]
  R2 = Resistor [tolerance=±5% resistance=10k package="0805 [SMD]"]

nets:
  GND: Arduino_Micro.GND, Easy_Driver.GND, J1.GND, R1.Pin_0, R2.Pin_0
  N1: Arduino_Micro.D2, Easy_Driver.DIR
  N2: Arduino_Micro.D3, Easy_Driver.STEP
  N3: Arduino_Micro.D4, Easy_Driver.MS1
  N4: Arduino_Micro.D5, Easy_Driver.ENABLE
  N5: Arduino_Micro.D6, Easy_Driver.MS2
  N6: Arduino_Micro.D7, JP3.2, R2.Pin_1
  N7: Arduino_Micro.D8, JP3.4, R1.Pin_1
  N8: Arduino_Micro.5V, JP3.1, JP3.3
  N9: Easy_Driver.V+, J1.PWR
  N10: Easy_Driver.OUT2A, JP2.1
  N11: Easy_Driver.OUT2B, JP2.2
  N12: Easy_Driver.OUT1A, JP2.3
  N13: Easy_Driver.OUT1B, JP2.4

notes:
  LiDAR v1.0
  motor
  limit switches
  5V
  GND
  D2
  D3
  D4
  D5
  D6
  D7
  D8
  Step
  Dir
  MS1
  Sleep
  A+
  A-
  B+
  B-
  PFD
  RST
  Enable
  MS2
  M+
  R1
  R2
  VIN
  TX1
  RX0
